# Fritzing sketch Radar (saved by Fritzing 0.9.2b)

parts:
  Componente1 = SRF05 Ultrasonic Rangefinder
  SERVO1 = Tower Pro SG90 servo [part_number=101246]
  Componente2 = Arduino Uno (Rev3)

nets:
  VCC: Componente1.VCC, SERVO1.+5V, Componente2.5V
  N1: Componente1.Trig, Componente2.D10_PWM/SS
  N2: Componente1.Echo, Componente2.D11_PWM/MOSI
  GND: Componente1.GND, SERVO1.GND, Componente2.GND
  N3: SERVO1.Signal, Componente2.D12/MISO

notes:
  12
  Trig -> 10
  Echo -> 11

custom parts:
  Tower Pro SG90 servo: Original file by John De Cristofaro http://www.adafruit.com/products/1449 Adafruit Feedback Servo (Small) Edited by: e-radionica.com 28/9/2015
